# Fritzing sketch protoboard (saved by Fritzing 0.9.0b)
breadboards: 1

parts:
  Raspberry_Pi1 = Raspberry Pi B rev2
  S1 = Momentary Switch [package=ksa_sealed_tac_switch]
  LED1 = smd LED [color="Red (633nm)" package="0805 [SMD]"]
  R1 = Resistor [tolerance=±5% resistance=180 package=THT]

nets:
  N1: Raspberry_Pi1.GND, S1.3, R1.Pin_0
  N2: Raspberry_Pi1.GPIO_23, S1.1
  N3: Raspberry_Pi1.GPIO_17, LED1.anode
  N4: LED1.cathode, R1.Pin_1
